# Fritzing sketch wemosPrinter (saved by Fritzing 0.9.4)

parts:
  WeMos_D1_Mini1 = WeMos D1 Mini
  Part1 = Thermal Printer

nets:
  N1: WeMos_D1_Mini1.5V, Part1.VH
  N2: WeMos_D1_Mini1.D4, Part1.RXD
  N3: WeMos_D1_Mini1.G, Part1.GND#0
